# Fritzing sketch UbiCaneSketch 1 (saved by Fritzing 0.9.3b)
circuit board: 9cm x 3.6cm
breadboards: 1

parts:
  Componente1 = Triple Axis Accelerometer Breakout - ADXL335
  J1 = Infrared Proximity Sensor
  J2 = Piezo Speaker
  J3 = Basic Servo
  R1 = Resistor [tolerance=±5% resistance=330 package=THT]
  R2 = Photocell (LDR) [package=THT]
  LED1 = LED - 5mm [color="Red (633nm)" package="5 mm [THT]"]
  Componente2 = Arduino Nano (Rev3.0)
  R3 = Resistor [tolerance=±5% resistance=10k package=THT]
  Q2 = PHOTOTRANSISTOR REFLECTIVE OBJECT SENSOR [package=qrb1114-side]
  R4 = Resistor [tolerance=±5% resistance=4.7k package=THT]
  R5 = Resistor [tolerance=±5% resistance=330 package=THT]
  VCC1 = Battery block 9V

nets:
  N1: Componente1.ST, Componente2.A0
  N2: Componente1.ZOUT, Componente2.A1
  N3: Componente1.YOUT, Componente2.A2
  N4: Componente1.XOUT, Componente2.A3
  GND: Componente1.GND, J1.GND, J2.pin1, J3.gnd, R2.pin_0, LED1.cathode, Componente2.GND, Q2.A, Q2.E, VCC1.-
  VCC: Componente1.VCC, J1.Vcc, J3.vcc, R1.Pin_0, Componente2.5V, R3.Pin_0, R4.Pin_0
  N5: J1.Vout, Componente2.D5
  N6: J2.pin2, Componente2.D12/MISO
  N7: J3.pulse, Componente2.D11/MOSI
  N8: R1.Pin_1, Q2.K
  N9: R2.pin_1, Componente2.D10, R4.Pin_1
  N10: LED1.anode, R5.Pin_1
  N11: Componente2.D7, R5.Pin_0
  N12: Componente2.D9, R3.Pin_1, Q2.C
  N13: Componente2.VIN, VCC1.+
