# Fritzing sketch termometro_sketch01 (saved by Fritzing 0.9.3b)
breadboards: 1

parts:
  R1 = Resistor [tolerance=±5% resistance=220 package=THT]
  R2 = Photocell (LDR) [package=THT]  # not connected
  T1 = LM35 Temperature Sensor [package="TO92 [THT]"]
  J1 = Piezo Speaker
  Componente1 = Arduino Uno (Rev3)
  R3 = Photocell (LDR) [package=THT]
  R4 = Resistor [tolerance=±5% resistance=220 package=THT]

nets:
  N1: R1.Pin_0, Componente1.D5_PWM
  N2: R1.Pin_1, T1.+Vs
  GND: T1.GND, J1.pin1, Componente1.GND, R3.pin_1
  N3: J1.pin2, Componente1.D8
  N4: Componente1.D6_PWM, R4.Pin_0
  N5: R3.pin_0, R4.Pin_1
